// Logisim project Cache.circ as structural Verilog: 8 circuits, main circuit main
module main (
  input  EnableTestHalting,
  output [9:0] CorrectCounter,
  output [9:0] HitCounter,
  output [9:0] MissCounter,
  output [9:0] TestNumber,
  output [7:0] ByteRead,
  output [7:0] CorrectByteRead,
  output Halt
);

  wire and_3_out, and_4_out, and_5_out, CLK, CmdIsRead, Correct, CpuRead, CpuWrite, DidContain, HaltTesting,
       MaxItersReached, MemRead, MemWrite, not_1_out, not_2_out, not_4_out, NotDoneTesting, Ok2Count,
       or_1_out, Ready;
  wire [7:0] CpuWriteValue, MemAddress;
  wire [9:0] CpuAddress;
  wire [31:0] Line2Mem, LineFromMem;

  not not_1 (not_1_out, Ready);
  Clock clock_1 (.out(CLK));
  or or_1 (or_1_out, MaxItersReached, Ready);
  Counter #(.width(4), .max('h9)) MaxClocks (
    .load(Ready), .D(4'b0001), .count(not_1_out), .carry(MaxItersReached), .clk(CLK));  // open: Q, clr
  and and_1 (HaltTesting, EnableTestHalting, CmdIsRead, not_2_out);
  not not_2 (not_2_out, Correct);
  not not_3 (NotDoneTesting, Halt);
  Inputs inputs_1 (
    .HaltTesting(HaltTesting), .Ready(or_1_out), .CLK(CLK), .Done(Halt), .Read(CpuRead), .Write(CpuWrite),
    .Address(CpuAddress), .Value(CpuWriteValue), .TestNumber(TestNumber));
  Cache cache_1 (
    .CpuAddress(CpuAddress), .CpuRead(CpuRead), .CpuWrite(CpuWrite), .CpuWriteValue(CpuWriteValue),
    .CLK(CLK), .Ready(Ready), .isFound(DidContain), .ByteRead(ByteRead), .MemAddress(MemAddress),
    .MemRead(MemRead), .MemWrite(MemWrite), .LineFromMem(LineFromMem), .Line2Mem(Line2Mem));
  // Probe on CpuRead
  // Probe on CpuWrite
  // Probe on CpuAddress
  // Probe on CpuWriteValue
  // Probe on TestNumber
  // Probe on CorrectByteRead
  // Probe on Correct
  // Probe on Ready
  // Probe on DidContain
  // Probe on ByteRead
  // Probe on MemAddress
  // Probe on MemRead
  // Probe on MemWrite
  // Probe on HitCounter
  // Probe on LineFromMem
  // Probe on Line2Mem
  not not_4 (not_4_out, HaltTesting);
  RAM #(.dataWidth(32), .bus("separate")) ram_1 (
    .addr(MemAddress), .din(Line2Mem), .data(LineFromMem), .str(MemWrite), .clk(CLK), .ld(MemRead));  // open: sel, clr
  and and_2 (Ok2Count, Ready, not_4_out, NotDoneTesting);
  and and_3 (and_3_out, Correct, Ok2Count);
  and and_4 (and_4_out, DidContain, Ok2Count);
  and and_5 (and_5_out, MemRead, NotDoneTesting);
  Checker checker_1 (
    .TestNumber(TestNumber), .YourByteRead(ByteRead), .CmdIsRead(CmdIsRead),
    .CorrectByteRead(CorrectByteRead), .Correct(Correct));
  Counter #(.width(10), .max('h3ff)) u_CorrectCounter (
    .count(and_3_out), .Q(CorrectCounter), .clk(CLK));  // open: load, D, carry, clr
  Counter #(.width(10), .max('h3ff)) u_HitCounter (
    .count(and_4_out), .Q(HitCounter), .clk(CLK));  // open: load, D, carry, clr
  Counter #(.width(10), .max('h3ff)) u_MissCounter (
    .count(and_5_out), .Q(MissCounter), .clk(CLK));  // open: load, D, carry, clr
  // Probe on CorrectCounter
  // Probe on HitCounter
  // Probe on MissCounter

  // Other names for the same wires on the sheet: DoneTesting = Halt

  // Notes on the sheet:
  //   Your Answer Inside Here
endmodule

module Cache (
  input  [9:0] CpuAddress,
  input  CpuRead,
  input  CpuWrite,
  input  [7:0] CpuWriteValue,
  input  CLK,
  input  [31:0] LineFromMem,
  output Ready,
  output isFound,
  output [7:0] ByteRead,
  output [7:0] MemAddress,
  output MemRead,
  output MemWrite,
  output [31:0] Line2Mem
);

  wire containa, containb, dirty, dirtya, dirtyb, DoesContain, isdirty, nand_1_out, nand_2_out, nand_3_out,
       nand_4_out, nand_5_out, nand_6_out, nand_7_out, nand_8_out, nand_9_out, nand_10_out, nand_11_out,
       nand_12_out, nand_13_out, nand_14_out, nand_15_out, nand_16_out, nand_17_out, nand_18_out,
       nand_19_out, nand_20_out, nand_21_out, nand_22_out, nand_23_out, nand_24_out, nand_25_out,
       nand_26_out, nand_27_out, nand_28_out, nand_29_out, nand_30_out, nand_31_out, nand_32_out,
       nand_33_out, nand_34_out, nand_35_out, nand_36_out, nand_37_out, nand_38_out, nand_39_out,
       nand_40_out, nand_41_out, nand_42_out, nand_43_out, nand_44_out, nand_45_out, nand_46_out,
       nand_47_out, nand_48_out, nand_49_out, nand_50_out, nand_51_out, nand_52_out, nand_53_out,
       nand_54_out, nand_55_out, nand_56_out, nand_57_out, nand_58_out, nand_59_out, nand_60_out,
       nand_61_out, nand_63_out, nand_64_out, nand_65_out, nand_66_out, nand_67_out, nand_68_out,
       nand_69_out, nand_70_out, nand_71_out, nand_72_out, nand_73_out, nand_74_out, nand_76_out, newAge,
       newDirty, newTag, newValid, normAge, outread, outwrite, saveInputs, saveLine, seta, setb, starta,
       startb, startContained, valid, valida, validb, write, writevalue;
  wire [2:0] fsm_1_n0, nand_77_out, stateA, statea_t;
  wire [6:0] ptaga, ptagb;
  wire [7:0] readbytea, readbyteb, temp, writetocpu;
  wire [9:0] addr;
  wire [31:0] readlinea, readlineb;

  Register writeVal (.D(CpuWriteValue), .en(saveInputs), .Q(writetocpu), .clk(CLK));  // open: clr
  Register #(.width(1)) read (.D(CpuRead), .en(saveInputs), .Q(outread), .clk(CLK));  // open: clr
  Register #(.width(10)) address (.D(CpuAddress), .en(saveInputs), .Q(addr), .clk(CLK));  // open: clr
  Demultiplexer #(.enable("false")) demultiplexer_1 (.out0(seta), .out1(setb), .in(1'b1), .sel(addr[2]));
  Register #(.width(1)) u_write (.D(CpuWrite), .en(saveInputs), .Q(outwrite), .clk(CLK));  // open: clr
  FSM fsm_1 (
    .p2(statea_t[2]), .p1(statea_t[1]), .p0(statea_t[0]), .CpuRead(outread), .CpuWrite(outwrite),
    .isFound(isFound), .dirty(isdirty), .n2(fsm_1_n0[2]), .n1(fsm_1_n0[1]), .n0(fsm_1_n0[0]), .ready(Ready),
    .normAge(normAge), .saveInputs(saveInputs), .startContained(startContained), .memRead(MemRead),
    .memWrite(MemWrite), .valid(valid), .newDirty(dirty));
  or or_1 (starta, normAge, seta);
  or or_2 (startb, normAge, setb);
  Register #(.width(3)) State (.D(fsm_1_n0), .en(1'b1), .Q(statea_t), .clk(CLK));  // open: clr
  set set_1 (
    .start(starta), .tag(addr[9:3]), .valid(valid), .dirty(dirty), .newTag(newTag), .newAge(newAge),
    .newValid(newValid), .newDirty(newDirty), .saveLine(saveLine), .normAge(normAge), .offset(addr[1:0]),
    .LineFromMem(LineFromMem), .write(write), .WriteVal(writevalue), .CpuWriteValue(writetocpu), .CLK(CLK),
    .currTag(ptaga), .isValid(valida), .isDirty(dirtya), .LineRead(readlinea), .ByteRead(readbytea),
    .DidContain(containa));
  set set_2 (
    .start(startb), .tag(addr[9:3]), .valid(valid), .dirty(dirty), .newTag(newTag), .newAge(newAge),
    .newValid(newValid), .newDirty(newDirty), .saveLine(saveLine), .normAge(normAge), .offset(addr[1:0]),
    .LineFromMem(LineFromMem), .write(write), .WriteVal(writevalue), .CpuWriteValue(writetocpu), .CLK(CLK),
    .currTag(ptagb), .isValid(validb), .isDirty(dirtyb), .LineRead(readlineb), .ByteRead(readbyteb),
    .DidContain(containb));
  Multiplexer #(.width(8), .enable("false")) multiplexer_1 (
    .in0({ptaga, 1'b0}), .in1({ptagb, 1'b1}), .out(temp), .sel(addr[2]));
  Multiplexer #(.width(32), .enable("false")) multiplexer_2 (
    .in0(readlinea), .in1(readlineb), .out(Line2Mem), .sel(addr[2]));
  Multiplexer #(.enable("false")) multiplexer_3 (.in0(dirtya), .in1(dirtyb), .out(isdirty), .sel(addr[2]));
  Multiplexer #(.width(8), .enable("false")) multiplexer_4 (
    .in0(readbytea), .in1(readbyteb), .out(ByteRead), .sel(addr[2]));
  Multiplexer #(.width(8), .enable("false")) multiplexer_5 (
    .in0(addr[9:2]), .in1(temp), .out(MemAddress), .sel(MemWrite));
  Multiplexer #(.enable("false")) multiplexer_6 (.in0(containa), .in1(containb), .out(DoesContain), .sel(addr[2]));
  Register #(.width(1)) DidContain (.D(DoesContain), .en(startContained), .Q(isFound), .clk(CLK));  // open: clr
  nand nand_1 (nand_1_out, outread, outread);
  nand nand_2 (nand_2_out, outwrite, outwrite);
  nand nand_3 (nand_3_out, isFound, isFound);
  nand nand_4 (nand_4_out, isdirty, isdirty);
  nand nand_5 (nand_5_out, stateA[1], stateA[1]);
  nand nand_6 (nand_6_out, outread, outread);
  nand nand_7 (nand_7_out, stateA[1], stateA[1]);
  nand nand_8 (nand_8_out, outwrite, outwrite);
  nand nand_9 (nand_9_out, stateA[2], stateA[2]);
  nand nand_10 (nand_10_out, stateA[1], stateA[1]);
  nand nand_11 (nand_11_out, stateA[0], stateA[0]);
  nand nand_12 (nand_12_out, outread, outread);
  nand nand_13 (nand_13_out, stateA[2], stateA[2]);
  nand nand_14 (nand_14_out, isFound, isFound);
  nand nand_15 (nand_15_out, isdirty, isdirty);
  nand nand_16 (nand_16_out, stateA[2], stateA[2]);
  nand nand_17 (nand_17_out, isFound, isFound);
  nand nand_18 (nand_18_out, isdirty, isdirty);
  nand nand_19 (nand_19_out, stateA[2], stateA[2]);
  nand nand_20 (nand_20_out, stateA[2], stateA[2]);
  nand nand_21 (nand_21_out, isFound, isFound);
  nand nand_22 (nand_22_out, isdirty, isdirty);
  nand nand_23 (nand_23_out, stateA[2], stateA[2]);
  nand nand_24 (nand_24_out, isFound, isFound);
  nand nand_25 (nand_25_out, isdirty, isdirty);
  nand nand_26 (nand_26_out, stateA[2], stateA[2]);
  nand nand_27 (nand_27_out, stateA[0], stateA[0]);
  nand nand_28 (nand_28_out, stateA[0], stateA[0]);
  nand nand_29 (nand_29_out, outread, outread);
  nand nand_30 (nand_30_out, nand_1_out, nand_2_out);
  nand nand_31 (nand_31_out, outread, outwrite);
  nand nand_32 (nand_32_out, stateA[1], nand_3_out, nand_4_out);
  nand nand_33 (nand_33_out, stateA[2], stateA[1]);
  nand nand_34 (nand_34_out, stateA[2], stateA[2]);
  nand nand_35 (nand_35_out, stateA[0], stateA[0]);
  nand nand_36 (nand_36_out, stateA[0], stateA[0]);
  nand nand_37 (nand_37_out, outread, outread);
  nand nand_38 (nand_38_out, stateA[2], stateA[2]);
  nand nand_39 (nand_39_out, nand_9_out, stateA[1], stateA[0]);
  nand nand_40 (nand_40_out, stateA[2], nand_10_out);
  nand nand_41 (nand_41_out, stateA[2], nand_11_out, nand_12_out);
  nand nand_42 (nand_42_out, stateA[1], stateA[1]);
  nand nand_43 (nand_43_out, stateA[0], stateA[0]);
  nand nand_44 (nand_44_out, stateA[1], stateA[1]);
  nand nand_45 (nand_45_out, stateA[0], stateA[0]);
  nand nand_46 (nand_46_out, stateA[0], stateA[0]);
  nand nand_47 (nand_47_out, outread, outread);
  nand nand_48 (nand_48_out, stateA[2], stateA[2]);
  nand nand_49 (nand_49_out, stateA[1], stateA[1]);
  nand nand_50 (nand_50_out, stateA[0], stateA[0]);
  nand nand_51 (nand_51_out, stateA[1], stateA[1]);
  nand nand_52 (nand_52_out, stateA[1], stateA[1]);
  nand nand_53 (nand_53_out, stateA[0], stateA[0]);
  nand nand_54 (nand_54_out, stateA[1], stateA[1]);
  nand nand_55 (nand_55_out, stateA[0], stateA[0]);
  nand nand_56 (nand_56_out, nand_26_out, stateA[1], nand_27_out);
  nand nand_57 (nand_57_out, nand_5_out, stateA[0], nand_6_out, outwrite);
  nand nand_58 (nand_58_out, nand_7_out, stateA[0], outread, nand_8_out);
  nand nand_59 (nand_59_out, nand_34_out, stateA[1], nand_35_out);
  nand nand_60 (nand_60_out, stateA[1], nand_36_out, nand_37_out);
  nand nand_61 (nand_61_out, nand_38_out, stateA[1], isFound);
  nand nand_62 (nand_77_out[2], nand_39_out, nand_40_out, nand_41_out);
  nand nand_63 (nand_63_out, nand_13_out, stateA[1], stateA[0], nand_14_out, nand_15_out);
  nand nand_64 (nand_64_out, stateA[2], nand_42_out, nand_43_out);
  nand nand_65 (nand_65_out, nand_16_out, stateA[1], stateA[0], nand_17_out, nand_18_out);
  nand nand_66 (nand_66_out, stateA[2], nand_44_out, nand_45_out);
  nand nand_67 (nand_67_out, stateA[2], nand_46_out, nand_47_out);
  nand nand_68 (nand_68_out, nand_48_out, nand_49_out, nand_50_out);
  nand nand_69 (nand_69_out, nand_19_out, stateA[1], stateA[0], isFound);
  nand nand_70 (nand_70_out, stateA[2], nand_51_out, stateA[0]);
  nand nand_71 (nand_71_out, nand_20_out, stateA[1], stateA[0], nand_21_out, nand_22_out);
  nand nand_72 (nand_72_out, stateA[2], nand_52_out, nand_53_out);
  nand nand_73 (nand_73_out, nand_23_out, stateA[1], stateA[0], nand_24_out, nand_25_out);
  nand nand_74 (nand_74_out, stateA[2], nand_54_out, nand_55_out);
  nand nand_75 (saveLine, nand_56_out, nand_56_out);
  nand nand_76 (nand_76_out, stateA[2], stateA[1], nand_28_out, nand_29_out);
  nand nand_77 (nand_77_out[0], stateA[0], nand_30_out, nand_31_out, nand_32_out, nand_33_out);
  nand nand_78 (nand_77_out[1], nand_57_out, nand_58_out, nand_59_out, nand_60_out, nand_61_out);
  nand nand_79 (newTag, nand_63_out, nand_64_out);
  nand nand_80 (newDirty, nand_65_out, nand_66_out, nand_67_out);
  nand nand_81 (newAge, nand_68_out, nand_69_out, nand_70_out);
  nand nand_82 (newValid, nand_71_out, nand_72_out);
  nand nand_83 (write, nand_73_out, nand_74_out);
  nand nand_84 (writevalue, nand_76_out, nand_76_out);
  Register #(.width(3)) State_2 (.D(nand_77_out), .en(1'b1), .Q(stateA), .clk(CLK));  // open: clr

  // Other names for the same wires on the sheet: offset[1:0] = addr[1:0]; set = addr[2]; tag[6:0] = addr[9:3];
  //   MemAddr[7:0] = MemAddress

  // Notes on the sheet:
  //   Address Bits = 10
  //   Line Size = 4
  //   W = 3
  //   Num Sets = 2
  //   C =4*3*2 = 24bytes
  //   Tag bits = 7
endmodule

module Inputs (
  input  HaltTesting,
  input  Ready,
  input  CLK,
  output Done,
  output Read,
  output Write,
  output [9:0] Address,
  output [7:0] Value,
  output [9:0] TestNumber
);

  wire and_1_out, not_1_out, not_2_out;

  not not_1 (not_1_out, HaltTesting);
  not not_2 (not_2_out, Done);
  Counter #(.width(10), .max('h3ff), .ongoal("stay")) u_TestNumber (
    .count(and_1_out), .Q(TestNumber), .clk(CLK));  // open: load, D, carry, clr
  and and_1 (and_1_out, not_1_out, Ready, not_2_out);
  ROM #(.addrWidth(10), .dataWidth(21)) rom_1 (
    .addr(TestNumber), .data({Done, Read, Write, Address, Value}));  // open: sel

  // Notes on the sheet:
  //   contents of rom_1 (hex, n*v repeats v):
  //   82420 407fd 41ec2 806f9 818dd 82ce4 42e75 8140f 80104 42b6e 42e0e 81cfd 81676 81d94 81a33 82897
  //   82faa 42061 412ff 42511 40fce 42a58 423bf 81c37 821c9 41f0f 4029d 42957 82074 80c76 420b0 41d89
  //   81842 81b1c 41766 41fb6 41600 41d0e 8285a 80582 82b24 801e7 8117f 4075e 41223 80a82 82a8b 41da4
  //   41e3a 813c5 41a60 40681 826dd 80e09 40912 81cda 828e6 8210f 42ba4 40398 80d18 40427 41351 42481
  //   80013 824eb 82d13 40cb1 80ddd 81f35 412ff 814cd 40150 81445 41b6d 42b31 423b0 42278 82e14 80856
  //   8226d 41582 415ae 81278 40835 402d0 8184b 8153a 40472 811ba 4243a 41137 81206 805d3 80260 825d7 0
  //   100000
endmodule

module Checker (
  input  [9:0] TestNumber,
  input  [7:0] YourByteRead,
  output CmdIsRead,
  output [7:0] CorrectByteRead,
  output Correct
);

  wire comparator_1_eq;
  wire [9:0] subtractor_1_out;

  // Probe on TestNumber
  Subtractor #(.width(10)) subtractor_1 (.a(TestNumber), .b(10'h1), .out(subtractor_1_out));  // open: bin, bout
  ROM #(.addrWidth(10), .dataWidth(9)) rom_1 (
    .addr(subtractor_1_out), .data({CmdIsRead, CorrectByteRead}));  // open: sel
  Comparator #(.mode("unsigned")) comparator_1 (
    .a(YourByteRead), .b(CorrectByteRead), .eq(comparator_1_eq));  // open: gt, lt
  and and_1 (Correct, comparator_1_eq, CmdIsRead);

  // Other names for the same wires on the sheet: Test_Number[9:0] = TestNumber

  // Notes on the sheet:
  //   Read Solutions
  //   contents of rom_1 (hex, n*v repeats v):
  //   124 fd c2 106 118 12c 75 114 101 6e e 11c 116 11d 11a 128 12f 61 ff 11 ce 58 bf 11c 121 f 9d 57 161
  //   10c b0 89 118 11b 66 b6 0 e 128 105 16e 101 111 5e 23 10a 158 a4 3a 113 60 81 126 10e 12 11c 128 121
  //   a4 98 10d 27 51 81 100 181 12d b1 10d 1b6 ff 114 50 114 6d 31 b0 78 10e 108 178 82 ae 1ff 35 d0 118
  //   1ae 72 111 3a 37 1ff 105 1d0 111
endmodule

module FSM (
  input  p2,
  input  p1,
  input  p0,
  input  CpuRead,
  input  CpuWrite,
  input  isFound,
  input  dirty,
  output n2,
  output n1,
  output n0,
  output ready,
  output normAge,
  output saveInputs,
  output startContained,
  output memRead,
  output memWrite,
  output valid,
  output newDirty
);

  wire nand_1_out, nand_2_out, nand_3_out, nand_4_out, nand_5_out, nand_6_out, nand_7_out, nand_8_out,
       nand_9_out, nand_10_out, nand_11_out, nand_12_out, nand_13_out, nand_14_out, nand_15_out, nand_16_out,
       nand_17_out, nand_18_out, nand_19_out, nand_20_out, nand_21_out, nand_22_out, nand_23_out,
       nand_24_out, nand_25_out, nand_26_out, nand_27_out, nand_28_out, nand_29_out, nand_30_out,
       nand_31_out, nand_32_out, nand_33_out, nand_34_out, nand_35_out, nand_36_out, nand_37_out,
       nand_38_out, nand_39_out, nand_40_out, nand_41_out, nand_42_out, nand_43_out, nand_44_out,
       nand_45_out, nand_46_out, nand_47_out, nand_48_out, nand_49_out, nand_50_out, nand_51_out,
       nand_52_out, nand_53_out, nand_54_out, nand_55_out, nand_56_out, nand_57_out, nand_58_out,
       nand_59_out, nand_60_out, nand_61_out, nand_62_out, nand_63_out, nand_64_out, nand_65_out,
       nand_66_out, nand_67_out, nand_68_out, nand_69_out, nand_70_out, nand_71_out;

  nand nand_1 (nand_1_out, p2, p2);
  nand nand_2 (nand_2_out, p1, p1);
  nand nand_3 (nand_3_out, p0, p0);
  nand nand_4 (nand_4_out, CpuRead, CpuRead);
  nand nand_5 (nand_5_out, p1, p1);
  nand nand_6 (nand_6_out, CpuRead, CpuRead);
  nand nand_7 (nand_7_out, p1, p1);
  nand nand_8 (nand_8_out, CpuWrite, CpuWrite);
  nand nand_9 (nand_9_out, p2, p2);
  nand nand_10 (nand_10_out, p0, p0);
  nand nand_11 (nand_11_out, p0, p0);
  nand nand_12 (nand_12_out, CpuRead, CpuRead);
  nand nand_13 (nand_13_out, p2, p2);
  nand nand_14 (nand_14_out, CpuRead, CpuRead);
  nand nand_15 (nand_15_out, CpuWrite, CpuWrite);
  nand nand_16 (nand_16_out, isFound, isFound);
  nand nand_17 (nand_17_out, dirty, dirty);
  nand nand_18 (nand_18_out, p2, p2);
  nand nand_19 (nand_19_out, p1, p1);
  nand nand_20 (nand_20_out, p2, p2);
  nand nand_21 (nand_21_out, p1, p1);
  nand nand_22 (nand_22_out, p0, p0);
  nand nand_23 (nand_23_out, p2, p2);
  nand nand_24 (nand_24_out, p1, p1);
  nand nand_25 (nand_25_out, p0, p0);
  nand nand_26 (nand_26_out, p2, p2);
  nand nand_27 (nand_27_out, p1, p1);
  nand nand_28 (nand_28_out, CpuRead, CpuRead);
  nand nand_29 (nand_29_out, p2, p2);
  nand nand_30 (nand_30_out, p1, p1);
  nand nand_31 (nand_31_out, CpuWrite, CpuWrite);
  nand nand_32 (nand_32_out, p2, p2);
  nand nand_33 (nand_33_out, p0, p0);
  nand nand_34 (nand_34_out, p2, p2);
  nand nand_35 (nand_35_out, isFound, isFound);
  nand nand_36 (nand_36_out, dirty, dirty);
  nand nand_37 (nand_37_out, p1, p1);
  nand nand_38 (nand_38_out, p0, p0);
  nand nand_39 (nand_39_out, p2, p2);
  nand nand_40 (nand_40_out, isFound, isFound);
  nand nand_41 (nand_41_out, p2, p2);
  nand nand_42 (nand_42_out, isFound, isFound);
  nand nand_43 (nand_43_out, dirty, dirty);
  nand nand_44 (nand_44_out, p1, p1);
  nand nand_45 (nand_45_out, p0, p0);
  nand nand_46 (nand_46_out, p0, p0);
  nand nand_47 (nand_47_out, CpuRead, CpuRead);
  nand nand_48 (nand_48_out, nand_1_out, p1, p0);
  nand nand_49 (nand_49_out, p2, nand_2_out);
  nand nand_50 (nand_50_out, p2, nand_3_out, nand_4_out);
  nand nand_51 (nand_51_out, nand_5_out, p0, nand_6_out, CpuWrite);
  nand nand_52 (nand_52_out, nand_7_out, p0, CpuRead, nand_8_out);
  nand nand_53 (nand_53_out, nand_9_out, p1, nand_10_out);
  nand nand_54 (nand_54_out, p1, nand_11_out, nand_12_out);
  nand nand_55 (nand_55_out, nand_13_out, p1, isFound);
  nand nand_56 (nand_56_out, nand_14_out, nand_15_out);
  nand nand_57 (nand_57_out, CpuRead, CpuWrite);
  nand nand_58 (nand_58_out, p1, nand_16_out, nand_17_out);
  nand nand_59 (nand_59_out, p2, p1);
  nand nand_60 (nand_60_out, nand_18_out, nand_19_out, p0);
  nand nand_61 (nand_61_out, nand_20_out, nand_21_out, nand_22_out);
  nand nand_62 (nand_62_out, nand_23_out, nand_24_out, nand_25_out);
  nand nand_63 (nand_63_out, nand_26_out, nand_27_out, nand_28_out, CpuWrite);
  nand nand_64 (nand_64_out, nand_29_out, nand_30_out, CpuRead, nand_31_out);
  nand nand_65 (nand_65_out, nand_32_out, p1, nand_33_out);
  nand nand_66 (nand_66_out, nand_34_out, p1, p0, nand_35_out, nand_36_out);
  nand nand_67 (nand_67_out, p2, nand_37_out, nand_38_out);
  nand nand_68 (nand_68_out, nand_39_out, p1, p0, nand_40_out, dirty);
  nand nand_69 (nand_69_out, nand_41_out, p1, p0, nand_42_out, nand_43_out);
  nand nand_70 (nand_70_out, p2, nand_44_out, nand_45_out);
  nand nand_71 (nand_71_out, p2, p1, nand_46_out, nand_47_out);
  nand nand_72 (n2, nand_48_out, nand_49_out, nand_50_out);
  nand nand_73 (n1, nand_51_out, nand_52_out, nand_53_out, nand_54_out, nand_55_out);
  nand nand_74 (n0, p0, nand_56_out, nand_57_out, nand_58_out, nand_59_out);
  nand nand_75 (ready, nand_60_out, nand_60_out);
  nand nand_76 (normAge, nand_61_out, nand_61_out);
  nand nand_77 (saveInputs, nand_62_out, nand_63_out, nand_64_out);
  nand nand_78 (startContained, nand_65_out, nand_65_out);
  nand nand_79 (memRead, nand_66_out, nand_67_out);
  nand nand_80 (memWrite, nand_68_out, nand_68_out);
  nand nand_81 (valid, nand_69_out, nand_70_out);
  nand nand_82 (newDirty, nand_71_out, nand_71_out);
endmodule

module updateAge (
  input  [1:0] Index,
  input  [1:0] pAgea,
  input  [1:0] pAgeb,
  input  [1:0] pAgec,
  output [1:0] nAgea,
  output [1:0] nAgeb,
  output [1:0] nAgec
);

  wire comparator_1_eq, comparator_1_lt, comparator_2_eq, comparator_2_lt, comparator_3_eq, comparator_3_lt;
  wire [1:0] adder_1_out, adder_2_out, adder_3_out, makeNewAge, tAgea, tAgeb, tAgec;

  Multiplexer #(.select(2), .width(2), .enable("false")) multiplexer_1 (
    .in0(pAgea), .in1(pAgeb), .in2(pAgec), .out(makeNewAge), .sel(Index));  // open: in3
  Comparator #(.width(2), .mode("unsigned")) comparator_1 (
    .a(pAgea), .b(makeNewAge), .eq(comparator_1_eq), .lt(comparator_1_lt));  // open: gt
  Adder #(.width(2)) adder_1 (.a(pAgea), .b(2'b01), .out(adder_1_out));  // open: cin, cout
  Multiplexer #(.width(2), .enable("false")) multiplexer_2 (
    .in0(tAgea), .in1(adder_1_out), .out(nAgea), .sel(comparator_1_lt));
  Comparator #(.width(2), .mode("unsigned")) comparator_2 (
    .a(pAgeb), .b(makeNewAge), .eq(comparator_2_eq), .lt(comparator_2_lt));  // open: gt
  Adder #(.width(2)) adder_2 (.a(pAgeb), .b(2'b01), .out(adder_2_out));  // open: cin, cout
  Multiplexer #(.width(2), .enable("false")) multiplexer_3 (
    .in0(pAgea), .in1(2'b00), .out(tAgea), .sel(comparator_1_eq));
  Multiplexer #(.width(2), .enable("false")) multiplexer_4 (
    .in0(pAgeb), .in1(2'b00), .out(tAgeb), .sel(comparator_2_eq));
  Multiplexer #(.width(2), .enable("false")) multiplexer_5 (
    .in0(tAgeb), .in1(adder_2_out), .out(nAgeb), .sel(comparator_2_lt));
  Comparator #(.width(2), .mode("unsigned")) comparator_3 (
    .a(pAgec), .b(makeNewAge), .eq(comparator_3_eq), .lt(comparator_3_lt));  // open: gt
  Multiplexer #(.width(2), .enable("false")) multiplexer_6 (
    .in0(pAgec), .in1(2'b00), .out(tAgec), .sel(comparator_3_eq));
  Adder #(.width(2)) adder_3 (.a(pAgec), .b(2'b01), .out(adder_3_out));  // open: cin, cout
  Multiplexer #(.width(2), .enable("false")) multiplexer_7 (
    .in0(tAgec), .in1(adder_3_out), .out(nAgec), .sel(comparator_3_lt));
endmodule

module line (
  input  start,
  input  [6:0] tag,
  input  [1:0] age,
  input  valid,
  input  dirty,
  input  newTag,
  input  newAge,
  input  newValid,
  input  newDirty,
  input  [1:0] offset,
  input  [31:0] LineFromMem,
  input  write,
  input  wval,
  input  [7:0] CpuWriteValue,
  input  CLK,
  output [6:0] pTag,
  output [1:0] pAge,
  output isValid,
  output isDirty,
  output [31:0] currLine,
  output [7:0] ByteRead
);

  wire and_5_out, demultiplexer_1_out0, demultiplexer_1_out1, demultiplexer_1_out2, demultiplexer_1_out3,
       or_1_out, or_2_out, or_3_out, or_4_out, startAge, startDirty, startTag, startValid, startWrite;
  wire [7:0] _00, _01, _10, _11;

  and and_1 (startTag, start, newTag);
  and and_2 (startValid, start, newValid);
  and and_3 (startDirty, start, newDirty);
  Register #(.width(1)) Dirty_Bit (.D(dirty), .en(startDirty), .Q(isDirty), .clk(CLK));  // open: clr
  Register #(.width(7)) Tag_Bits (.D(tag), .en(startTag), .Q(pTag), .clk(CLK));  // open: clr
  Register #(.width(2)) u_Age (.D(age), .en(startAge), .Q(pAge), .clk(CLK));  // open: clr
  Register #(.width(1)) Valid_Bit (.D(valid), .en(startValid), .Q(isValid), .clk(CLK));  // open: clr
  and and_4 (startAge, start, newAge);
  and and_5 (and_5_out, start, wval);
  and and_6 (startWrite, start, write);
  Demultiplexer #(.select(2), .enable("false")) demultiplexer_1 (
    .out0(demultiplexer_1_out0), .out1(demultiplexer_1_out1), .out2(demultiplexer_1_out2),
    .out3(demultiplexer_1_out3), .in(and_5_out), .sel(offset));
  Register Val00 (.D(_00), .en(or_1_out), .Q(currLine[7:0]), .clk(CLK));  // open: clr
  or or_1 (or_1_out, startWrite, demultiplexer_1_out0);
  Register Val01 (.D(_01), .en(or_2_out), .Q(currLine[15:8]), .clk(CLK));  // open: clr
  or or_2 (or_2_out, startWrite, demultiplexer_1_out1);
  Multiplexer #(.width(8), .enable("false")) multiplexer_1 (
    .in0(LineFromMem[7:0]), .in1(CpuWriteValue), .out(_00), .sel(wval));
  Multiplexer #(.width(8), .enable("false")) multiplexer_2 (
    .in0(LineFromMem[15:8]), .in1(CpuWriteValue), .out(_01), .sel(wval));
  Register Val10 (.D(_10), .en(or_3_out), .Q(currLine[23:16]), .clk(CLK));  // open: clr
  or or_3 (or_3_out, startWrite, demultiplexer_1_out2);
  Register Val11 (.D(_11), .en(or_4_out), .Q(currLine[31:24]), .clk(CLK));  // open: clr
  or or_4 (or_4_out, startWrite, demultiplexer_1_out3);
  Multiplexer #(.width(8), .enable("false")) multiplexer_3 (
    .in0(LineFromMem[23:16]), .in1(CpuWriteValue), .out(_10), .sel(wval));
  Multiplexer #(.width(8), .enable("false")) multiplexer_4 (
    .in0(LineFromMem[31:24]), .in1(CpuWriteValue), .out(_11), .sel(wval));
  Multiplexer #(.select(2), .width(8), .enable("false")) multiplexer_5 (
    .in0(currLine[7:0]), .in1(currLine[15:8]), .in2(currLine[23:16]), .in3(currLine[31:24]), .out(ByteRead),
    .sel(offset));
endmodule

module set (
  input  start,
  input  [6:0] tag,
  input  valid,
  input  dirty,
  input  newTag,
  input  newAge,
  input  newValid,
  input  newDirty,
  input  saveLine,
  input  normAge,
  input  [1:0] offset,
  input  [31:0] LineFromMem,
  input  write,
  input  WriteVal,
  input  [7:0] CpuWriteValue,
  input  CLK,
  output [6:0] currTag,
  output isValid,
  output isDirty,
  output [31:0] LineRead,
  output [7:0] ByteRead,
  output DidContain
);

  wire comparator_1_eq, comparator_2_eq, comparator_3_eq, dirtya, dirtyb, dirtyc, founda, foundb, foundc,
       newDirty00, newDirty01, newDirty10, newTag00, newTag01, newTag10, newValid00, newValid01, newValid10,
       NotFound, olda, oldb, oldc, startStoreLine, valida, validb, validc, write00, write01, write10, wVal00,
       wVal01, wVal10;
  wire [1:0] multiplexer_1_out, multiplexer_2_out, multiplexer_3_out, multiplexer_4_out, multiplexer_5_out,
       nxtAgea, nxtAgeb, nxtAgec, oldest, pAgea, pAgeb, pAgec, SelectedLine, tAgea, tAgeb, tAgec;
  wire [6:0] pTaga, pTagb, pTagc;
  wire [7:0] bytea, byteb, bytec;
  wire [31:0] pLinea, pLineb, pLinec;

  line linea (
    .start(start), .tag(tag), .age(nxtAgea), .valid(valid), .dirty(dirty), .newTag(newTag00),
    .newAge(newAge), .newValid(newValid00), .newDirty(newDirty00), .offset(offset),
    .LineFromMem(LineFromMem), .write(write00), .wval(wVal00), .CpuWriteValue(CpuWriteValue), .CLK(CLK),
    .pTag(pTaga), .pAge(pAgea), .isValid(valida), .isDirty(dirtya), .currLine(pLinea), .ByteRead(bytea));
  line lineb (
    .start(start), .tag(tag), .age(nxtAgeb), .valid(valid), .dirty(dirty), .newTag(newTag01),
    .newAge(newAge), .newValid(newValid01), .newDirty(newDirty01), .offset(offset),
    .LineFromMem(LineFromMem), .write(write01), .wval(wVal01), .CpuWriteValue(CpuWriteValue), .CLK(CLK),
    .pTag(pTagb), .pAge(pAgeb), .isValid(validb), .isDirty(dirtyb), .currLine(pLineb), .ByteRead(byteb));
  and and_1 (startStoreLine, start, saveLine);
  line linec (
    .start(start), .tag(tag), .age(nxtAgec), .valid(valid), .dirty(dirty), .newTag(newTag10),
    .newAge(newAge), .newValid(newValid10), .newDirty(newDirty10), .offset(offset),
    .LineFromMem(LineFromMem), .write(write10), .wval(wVal10), .CpuWriteValue(CpuWriteValue), .CLK(CLK),
    .pTag(pTagc), .pAge(pAgec), .isValid(validc), .isDirty(dirtyc), .currLine(pLinec), .ByteRead(bytec));
  Comparator #(.width(7), .mode("unsigned")) comparator_1 (.a(pTagb), .b(tag), .eq(comparator_1_eq));  // open: gt, lt
  Comparator #(.width(7), .mode("unsigned")) comparator_2 (.a(pTaga), .b(tag), .eq(comparator_2_eq));  // open: gt, lt
  and and_2 (foundb, comparator_1_eq, validb);
  Comparator #(.width(7), .mode("unsigned")) comparator_3 (.a(pTagc), .b(tag), .eq(comparator_3_eq));  // open: gt, lt
  and and_3 (NotFound, ~founda, ~foundb, ~foundc);  // AND_Gate
  and and_4 (founda, comparator_2_eq, valida);
  and and_5 (foundc, comparator_3_eq, validc);
  Comparator #(.width(2), .mode("unsigned")) comparator_4 (.a(pAgeb), .b(2'b10), .eq(oldb));  // open: gt, lt
  Comparator #(.width(2), .mode("unsigned")) comparator_5 (.a(pAgec), .b(2'b10), .eq(oldc));  // open: gt, lt
  Comparator #(.width(2), .mode("unsigned")) comparator_6 (.a(pAgea), .b(2'b10), .eq(olda));  // open: gt, lt
  Multiplexer #(.width(2), .enable("false")) multiplexer_1 (
    .in0(oldest), .in1(2'b10), .out(multiplexer_1_out), .sel(foundc));
  Multiplexer #(.width(2), .enable("false")) multiplexer_2 (
    .in0(multiplexer_1_out), .in1(2'b01), .out(multiplexer_2_out), .sel(foundb));
  Multiplexer #(.width(2), .enable("false")) multiplexer_3 (
    .in0(2'b10), .in1(2'b10), .out(multiplexer_3_out), .sel(oldc));
  Multiplexer #(.width(2), .enable("false")) multiplexer_4 (
    .in0(multiplexer_2_out), .in1(2'b00), .out(multiplexer_4_out), .sel(founda));
  Multiplexer #(.width(2), .enable("false")) multiplexer_5 (
    .in0(multiplexer_3_out), .in1(2'b01), .out(multiplexer_5_out), .sel(oldb));
  updateAge updateage_1 (
    .Index(SelectedLine), .pAgea(pAgea), .pAgeb(pAgeb), .pAgec(pAgec), .nAgea(tAgea), .nAgeb(tAgeb),
    .nAgec(tAgec));
  Register #(.width(2)) indexOfLine (
    .D(multiplexer_4_out), .en(startStoreLine), .Q(SelectedLine), .clk(CLK));  // open: clr
  Multiplexer #(.width(2), .enable("false")) multiplexer_6 (
    .in0(multiplexer_5_out), .in1(2'b00), .out(oldest), .sel(olda));
  Multiplexer #(.width(2), .enable("false")) multiplexer_7 (.in0(tAgea), .in1(2'b00), .out(nxtAgea), .sel(normAge));
  Multiplexer #(.width(2), .enable("false")) multiplexer_8 (.in0(tAgeb), .in1(2'b01), .out(nxtAgeb), .sel(normAge));
  Multiplexer #(.width(2), .enable("false")) multiplexer_9 (.in0(tAgec), .in1(2'b10), .out(nxtAgec), .sel(normAge));
  Demultiplexer #(.select(2), .enable("false")) demultiplexer_1 (
    .out0(newTag00), .out1(newTag01), .out2(newTag10), .in(newTag), .sel(SelectedLine));  // open: out3
  Demultiplexer #(.select(2), .enable("false")) demultiplexer_2 (
    .out0(newDirty00), .out1(newDirty01), .out2(newDirty10), .in(newDirty), .sel(SelectedLine));  // open: out3
  Demultiplexer #(.select(2), .enable("false")) demultiplexer_3 (
    .out0(newValid00), .out1(newValid01), .out2(newValid10), .in(newValid), .sel(SelectedLine));  // open: out3
  Demultiplexer #(.select(2), .enable("false")) demultiplexer_4 (
    .out0(write00), .out1(write01), .out2(write10), .in(write), .sel(SelectedLine));  // open: out3
  Demultiplexer #(.select(2), .enable("false")) demultiplexer_5 (
    .out0(wVal00), .out1(wVal01), .out2(wVal10), .in(WriteVal), .sel(SelectedLine));  // open: out3
  Multiplexer #(.select(2), .width(7), .enable("false")) multiplexer_10 (
    .in0(pTaga), .in1(pTagb), .in2(pTagc), .out(currTag), .sel(SelectedLine));  // open: in3
  Multiplexer #(.select(2), .enable("false")) multiplexer_11 (
    .in0(valida), .in1(validb), .in2(validc), .out(isValid), .sel(SelectedLine));  // open: in3
  Multiplexer #(.select(2), .enable("false")) multiplexer_12 (
    .in0(dirtya), .in1(dirtyb), .in2(dirtyc), .out(isDirty), .sel(SelectedLine));  // open: in3
  Multiplexer #(.select(2), .width(32), .enable("false")) multiplexer_13 (
    .in0(pLinea), .in1(pLineb), .in2(pLinec), .out(LineRead), .sel(SelectedLine));  // open: in3
  Multiplexer #(.select(2), .width(8), .enable("false")) multiplexer_14 (
    .in0(bytea), .in1(byteb), .in2(bytec), .out(ByteRead), .sel(SelectedLine));  // open: in3
  not not_1 (DidContain, NotFound);
endmodule
