// Logisim project Vending.circ as structural Verilog: 5 circuits, main circuit main
module main (
  input  Halt_Enable
);

  wire and_2_out, CLK, Correct, Dime, Done_Testing, Give_Dime, Give_Merch, Give_Nickel, Halt, Nickel,
       not_1_out, not_2_out, not_3_out, Quarter, Sol_Give_Dime, Sol_Give_Merch, Sol_Give_Nickel;
  wire [8:0] counter_1_q, TestNumber;

  Clock clock_1 (.out(CLK));
  not not_1 (not_1_out, Correct);
  and and_1 (Halt, Halt_Enable, not_1_out);
  Inputs inputs_1 (
    .Halt(Halt), .CLK(CLK), .Quarter(Quarter), .Dime(Dime), .Nickel(Nickel), .TestNumber(TestNumber),
    .Done_Testing(Done_Testing));
  // Probe on Quarter
  // Probe on Dime
  // Probe on Nickel
  Vending vending_1 (
    .Quarter(Quarter), .Dime(Dime), .Nickel(Nickel), .CLK(CLK), .Give_Merchandise(Give_Merch),
    .Give_Dime(Give_Dime), .Give_Nickel(Give_Nickel));
  // Probe on Correct
  // Probe on Give_Merch
  // Probe on Sol_Give_Merch
  // Probe on Give_Dime
  // Probe on Sol_Give_Dime
  // Probe on Give_Nickel
  // Probe on Sol_Give_Nickel
  not not_2 (not_2_out, Halt);
  Checker checker_1 (
    .Give_Merch(Give_Merch), .Give_Dime(Give_Dime), .Give_Nickel(Give_Nickel), .TestNumber(TestNumber),
    .Correct(Correct), .Sol_Give_Merch(Sol_Give_Merch), .Sol_Give_Dime(Sol_Give_Dime),
    .Sol_Give_Nickel(Sol_Give_Nickel));
  and and_2 (and_2_out, Correct, not_2_out, not_3_out);
  not not_3 (not_3_out, Done_Testing);
  Counter #(.width(9), .max('h162), .ongoal("stay")) counter_1 (
    .count(and_2_out), .Q(counter_1_q), .clk(CLK));  // open: load, D, carry, clr
  // Probe on counter_1_q

  // Notes on the sheet:
  //   Max 354
endmodule

module Vending (
  input  Quarter,
  input  Dime,
  input  Nickel,
  input  CLK,
  output Give_Merchandise,
  output Give_Dime,
  output Give_Nickel
);

  wire [2:0] prevState, register_1_q;

  Register #(.width(3)) register_1 (.D(prevState), .Q(register_1_q), .clk(CLK));  // open: en, clr
  stateAssigning stateassigning_1 (
    .state0(register_1_q[2]), .state1(register_1_q[1]), .state2(register_1_q[0]), .quarter(Quarter),
    .dime(Dime), .nickel(Nickel), .give_merch(Give_Merchandise), .nickel_output(Give_Dime),
    .dime_output(Give_Nickel), .nextState0(prevState[2]), .nextState1(prevState[1]), .nextState2(prevState[0]));

  // Other names for the same wires on the sheet: give_merch = Give_Merchandise; Quater = Quarter
endmodule

module Inputs (
  input  Halt,
  input  CLK,
  output Quarter,
  output Dime,
  output Nickel,
  output [8:0] TestNumber,
  output Done_Testing
);

  wire not_1_out;

  not not_1 (not_1_out, Halt);
  Counter #(.width(9), .max('h162), .ongoal("stay")) counter_1 (
    .count(not_1_out), .Q(TestNumber), .carry(Done_Testing), .clk(CLK));  // open: load, D, clr
  ROM #(.addrWidth(9), .dataWidth(3)) rom_1 (.addr(TestNumber), .data({Quarter, Dime, Nickel}));  // open: sel

  // Notes on the sheet:
  //   contents of rom_1 (hex, n*v repeats v):
  //   1 0 1 0 1 0 1 0 1 0 1 0 1 0 1 0 1 0 1 0 1 0 2 0 1 0 1 0 1 0 1 0 1 0 4 0 1 0 1 0 1 0 1 0 2 0 1 0 1 0
  //   1 0 1 0 4 0 1 0 1 0 1 0 1 0 2 0 1 0 1 0 1 0 2 0 2 0 1 0 1 0 1 0 2 0 4 0 1 0 1 0 1 0 4 0 1 0 1 0 1 0
  //   1 0 2 0 1 0 1 0 1 0 2 0 2 0 1 0 1 0 1 0 2 0 4 0 1 0 1 0 2 0 2 0 1 0 1 0 2 0 4 0 1 0 1 0 4 0 1 0 1 0
  //   1 0 1 0 2 0 1 0 1 0 1 0 2 0 2 0 1 0 1 0 1 0 2 0 4 0 1 0 1 0 2 0 2 0 1 0 1 0 2 0 4 0 1 0 1 0 2 0 2 0
  //   1 0 2 0 2 0 2 0 1 0 2 0 2 0 4 0 1 0 2 0 4 0 1 0 4 0 1 0 1 0 1 0 1 0 2 0 1 0 1 0 1 0 2 0 2 0 1 0 1 0
  //   1 0 2 0 4 0 1 0 1 0 2 0 2 0 1 0 1 0 2 0 4 0 1 0 1 0 2 0 2 0 1 0 2 0 2 0 2 0 1 0 2 0 2 0 4 0 1 0 2 0
  //   4 0 1 0 1 0 2 0 2 0 1 0 2 0 2 0 2 0 1 0 2 0 2 0 4 0 2 0 2 0 2 0 2 0 2 0 4 0 2 0 4 0 1 0 4 0 2 0 4 0
  //   4 0 4
endmodule

module Checker (
  input  Give_Merch,
  input  Give_Dime,
  input  Give_Nickel,
  input  [8:0] TestNumber,
  output Correct,
  output Sol_Give_Merch,
  output Sol_Give_Dime,
  output Sol_Give_Nickel
);

  ROM #(.addrWidth(9), .dataWidth(3)) rom_1 (
    .addr(TestNumber), .data({Sol_Give_Merch, Sol_Give_Dime, Sol_Give_Nickel}));  // open: sel
  Comparator #(.width(3)) comparator_1 (
    .a({Sol_Give_Merch, Sol_Give_Dime, Sol_Give_Nickel}), .b({Give_Merch, Give_Dime, Give_Nickel}),
    .eq(Correct));  // open: gt, lt

  // Other names for the same wires on the sheet: Solution[2:0] = {Sol_Give_Merch, Sol_Give_Dime, Sol_Give_Nickel};
  //   Your_Answer[2:0] = {Give_Merch, Give_Dime, Give_Nickel}

  // Notes on the sheet:
  //   contents of rom_1 (hex, n*v repeats v):
  //   10*0 4 11*0 5 11*0 7 9*0 4 9*0 7 9*0 4 9*0 5 9*0 7 7*0 6 9*0 4 9*0 5 9*0 7 7*0 4 7*0 7 5*0 5 9*0 4
  //   9*0 5 9*0 7 7*0 4 7*0 7 7*0 4 7*0 5 7*0 7 5*0 6 0 0 0 4 9*0 4 9*0 5 9*0 7 7*0 4 7*0 7 7*0 4 7*0 5
  //   7*0 7 5*0 6 7*0 4 7*0 5 7*0 7 5*0 4 5*0 7 0 0 0 5 0 0 0 4 0 0 0 5 0 0 0 7
endmodule

module stateAssigning (
  input  state0,
  input  state1,
  input  state2,
  input  quarter,
  input  dime,
  input  nickel,
  output give_merch,
  output nickel_output,
  output dime_output,
  output nextState0,
  output nextState1,
  output nextState2
);

  wire and_1_out, and_2_out, and_3_out, and_4_out, and_5_out, and_6_out, and_7_out, and_8_out, and_9_out,
       and_10_out, and_11_out, and_12_out, and_13_out, and_14_out, and_15_out, and_16_out, and_17_out,
       and_18_out, and_19_out, and_20_out, and_21_out, and_22_out, and_23_out, and_24_out, and_25_out,
       and_26_out, and_27_out, and_28_out, and_29_out, and_30_out, and_31_out, not_1_out, not_2_out,
       not_3_out, not_4_out, not_5_out, not_6_out, not_7_out, not_8_out, not_9_out, not_10_out, not_11_out,
       not_12_out, not_13_out, not_14_out, not_15_out, not_16_out, not_17_out, not_18_out, not_19_out,
       not_20_out, not_21_out, not_22_out, not_23_out, not_24_out;

  and and_1 (and_1_out, state2, quarter);
  and and_2 (and_2_out, state1, quarter);
  and and_3 (and_3_out, state0, dime);
  and and_4 (and_4_out, state0, quarter);
  and and_5 (and_5_out, state0, state2, nickel);
  and and_6 (and_6_out, state0, state1, nickel);
  and and_7 (and_7_out, state0, state1, state2);
  and and_8 (and_8_out, state1, state2, quarter);
  and and_9 (and_9_out, state0, quarter);
  and and_10 (and_10_out, state0, state1, nickel);
  and and_11 (and_11_out, state0, state1, dime);
  and and_12 (and_12_out, state0, state1, state2);
  not not_1 (not_1_out, state2);
  not not_2 (not_2_out, state0);
  not not_3 (not_3_out, state1);
  not not_4 (not_4_out, state2);
  not not_5 (not_5_out, quarter);
  not not_6 (not_6_out, dime);
  not not_7 (not_7_out, nickel);
  not not_8 (not_8_out, state2);
  not not_9 (not_9_out, state0);
  not not_10 (not_10_out, state1);
  not not_11 (not_11_out, state0);
  not not_12 (not_12_out, state1);
  not not_13 (not_13_out, state2);
  not not_14 (not_14_out, state0);
  not not_15 (not_15_out, state1);
  not not_16 (not_16_out, quarter);
  not not_17 (not_17_out, dime);
  not not_18 (not_18_out, nickel);
  not not_19 (not_19_out, state2);
  not not_20 (not_20_out, state2);
  not not_21 (not_21_out, quarter);
  not not_22 (not_22_out, dime);
  not not_23 (not_23_out, nickel);
  not not_24 (not_24_out, state0);
  or or_1 (nickel_output, and_8_out, and_9_out, and_10_out, and_11_out, and_12_out);
  and and_13 (and_13_out, state1, not_1_out, quarter);
  and and_14 (and_14_out, state0, quarter);
  and and_15 (and_15_out, state0, state2, dime);
  and and_16 (and_16_out, state0, state1, nickel);
  and and_17 (and_17_out, state0, state1, dime);
  and and_18 (and_18_out, state0, state1, state2);
  and and_19 (and_19_out, not_2_out, not_3_out, not_4_out, quarter);
  and and_20 (and_20_out, state1, dime);
  and and_21 (and_21_out, state1, state2, nickel);
  and and_22 (and_22_out, state0, not_5_out, not_6_out, not_7_out);
  and and_23 (and_23_out, state0, not_8_out, nickel);
  and and_24 (and_24_out, not_9_out, not_10_out, dime);
  and and_25 (and_25_out, not_11_out, not_12_out, not_13_out, quarter);
  and and_26 (and_26_out, not_14_out, not_15_out, state2, nickel);
  and and_27 (and_27_out, state1, not_16_out, not_17_out, not_18_out);
  and and_28 (and_28_out, state1, not_19_out, nickel);
  and and_29 (and_29_out, not_20_out, nickel);
  and and_30 (and_30_out, state2, not_21_out, not_22_out, not_23_out);
  and and_31 (and_31_out, not_24_out, state2, dime);
  or or_2 (give_merch, and_1_out, and_2_out, and_3_out, and_4_out, and_5_out, and_6_out, and_7_out);
  or or_3 (dime_output, and_13_out, and_14_out, and_15_out, and_16_out, and_17_out, and_18_out);
  or or_4 (nextState0, and_19_out, and_20_out, and_21_out, and_22_out, and_23_out);
  or or_5 (nextState1, and_24_out, and_25_out, and_26_out, and_27_out, and_28_out);
  or or_6 (nextState2, and_29_out, and_30_out, and_31_out);
endmodule
